# Fritzing sketch SchemaElectStationOled_ArduiProMini (saved by Fritzing 0.9.3b)
circuit board: 8.46667cm x 5.64444cm
perfboards: 1

parts:
  Composant2 = Arduino Pro Mini v13
  T1 = LM35 Temperature Sensor [package="TO92 [THT]"]
  Grove1 = Grove OLED 128x96
  X1 = USB Connectors [package=usb-a-h]
  U1 = TEMPERATURE-SENSOR [package=to-92]
  R1 = Resistor [tolerance=±5% resistance=4.7k package=THT]

nets:
  VCC: Composant2.VCC, T1.+Vs, Grove1.VCC, X1.D+, U1.VCC, R1.Pin_1
  GND: Composant2.GND, T1.GND, Grove1.GND, X1.GND, U1.GND
  N1: Composant2.A4, Grove1.SCL
  N2: Composant2.A5, Grove1.SDA
  N3: Composant2.A0, T1.Vout
  N4: Composant2.D2, U1.ADJ, R1.Pin_0
